# Fritzing sketch Nano_BasicIO (saved by Fritzing 0.9.10b)
breadboards: 1

parts:
  M1 = Arduino Nano 33 IOT-tht
  U1 = POT [knob_status=50% power=0.5W package=pot_mammoth]
  LED1 = LED - 5mm [color="Red (633nm)" current=0.030 package="5 mm [THT]"]
  LED2 = RGB LED (com. cathode, rgb) [package="5 mm [THT]"]
  S1 = Pushbutton [package="[THT]"]
  S2 = Pushbutton [package="[THT]"]
  S3 = Pushbutton [package="[THT]"]
  S4 = Pushbutton [package="[THT]"]
  R1 = Resistor [tolerance=±5% power=0.25 resistance=220 package=THT]
  R2 = Resistor [tolerance=±5% power=0.25 resistance=220 package=THT]
  R3 = Resistor [tolerance=±5% power=0.25 resistance=220 package=THT]
  R4 = Resistor [tolerance=±5% power=0.25 resistance=220 package=THT]

nets:
  N1: M1.pin_2, U1.S
  N2: M1.pin_4, S1.Pin_3, S1.Pin_4
  N3: M1.pin_5, S2.Pin_3, S2.Pin_4
  N4: M1.pin_6, S3.Pin_3, S3.Pin_4
  N5: M1.pin_7, S4.Pin_3, S4.Pin_4
  N6: M1.pin_9, R4.Pin_0
  N7: M1.pin_11, U1.A
  N8: M1.pin_13, M1.pin_18
  N9: M1.pin_14, M1.pin_19, U1.E, LED1.cathode, LED2.common_cathode, S1.Pin_1, S1.Pin_2, S2.Pin_1, S2.Pin_2, S3.Pin_1, S3.Pin_2, S4.Pin_1, S4.Pin_2
  N10: M1.pin_28, R3.Pin_0
  N11: M1.pin_29, R2.Pin_0
  N12: M1.pin_30, R1.Pin_0
  N13: LED1.anode, R4.Pin_1
  N14: LED2.red_anode, R3.Pin_1
  N15: LED2.green_anode, R2.Pin_1
  N16: LED2.blue_anode, R1.Pin_1

notes:
  Long Leg of RGB LED in 45,
  Long Leg of 2-Pin LED in 49
  Arduino Column | Part | Destination Column
  2 | Power 3V | any on PWR + rail (red)
  4 | Blue Button | 19
  5 | Green Button | 24
  6 | Red Button | 29
  7 | Other Button | 34
  9 | Other LED | 49 [top]
  11 | Potentiometer | 55 [top]
  14 | GND | any on GND - rail (blue)
  1 [top] | Blue LED | 43 [top]
  2 [top] | Green LED | 44 [top]
  3 [top] | Red LED | 46 [top]

custom parts:
  Arduino Nano 33 IOT-tht: The Arduino Nano 33 IoT is the easiest and cheapest point of entry to enhance existing devices (and creating new ones) to be part of the IoT and designing pico-network applications. Whether you are looking at building a sensor network connected to your office or home router, or if you want to create a BLE device sending data to a cellphone, the Nano 33 IoT is your one-stop-solution for many of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
