# Fritzing sketch Nano_DrumMIDI (saved by Fritzing 0.9.10b)
breadboards: 1

parts:
  M1 = Arduino Nano 33 IOT-tht
  R1 = Resistor [tolerance=±5% power=0.25 resistance=220 package=THT]
  R2 = Resistor [tolerance=±5% resistance=220 package="2512 [SMD]"]
  J1 = Piezo Speaker
  S1 = Round Pushbutton
  R3 = Resistor [tolerance=±5% power=0.25 resistance=220 package=THT]
  R4 = Resistor [tolerance=±5% power=0.25 resistance=220 package=THT]
  R5 = Resistor [tolerance=±5% power=0.25 resistance=220 package=THT]
  R6 = Resistor [tolerance=±5% resistance=220 package="2512 [SMD]"]
  R7 = Resistor [tolerance=±5% resistance=220 package="2512 [SMD]"]
  R8 = Resistor [tolerance=±5% resistance=220 package="2512 [SMD]"]
  J2 = Piezo Speaker
  J3 = Piezo Speaker
  J4 = Piezo Speaker

nets:
  N1: M1.pin_4, R1.Pin_0
  N2: M1.pin_5, R3.Pin_0
  N3: M1.pin_6, R4.Pin_0
  N4: M1.pin_7, R5.Pin_0
  N5: M1.pin_8, S1.leg0
  N6: M1.pin_13, M1.pin_18
  N7: M1.pin_14, M1.pin_19, R2.Pin_0, J1.pin1, S1.leg1, R6.Pin_0, R7.Pin_0, R8.Pin_0, J2.pin1, J3.pin1, J4.pin1
  N8: R1.Pin_1, R2.Pin_1, J1.pin2
  N9: R3.Pin_1, R6.Pin_1, J2.pin2
  N10: R4.Pin_1, R7.Pin_1, J3.pin2
  N11: R5.Pin_1, R8.Pin_1, J4.pin2

notes:
  The blue resistors are the 100k ohm resistors (brown black black gold brown)
  The tan resistors are the 820k ohm resistors (grey red black orange brown)
  kick foot pedal button
  (ignore green pin of plug)

custom parts:
  Arduino Nano 33 IOT-tht: The Arduino Nano 33 IoT is the easiest and cheapest point of entry to enhance existing devices (and creating new ones) to be part of the IoT and designing pico-network applications. Whether you are looking at building a sensor network connected to your office or home router, or if you want to create a BLE device sending data to a cellphone, the Nano 33 IoT is your one-stop-solution for many of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
